// Digital circuit 5bit_Substract.dig as structural Verilog
module _5bit_Substract (
  input  [4:0] A,
  input  [4:0] B,
  output [4:0] S
);

  wire [4:0] B_inv;

  assign B_inv = ~B;  // Not not_1, 5 bits wide
  _5bit_Adder _5bit_adder_1 (.A(A), .B(B_inv), .Ci(1'b1), .S(S));  // open: Co
endmodule
