// Digital circuit 8bit_Adder.dig as structural Verilog
module _8bit_Adder (
  input  [7:0] A_7__0,
  input  [7:0] B_7__0,
  input  Cin,
  output [7:0] Sum_7__0,
  output Final_Cout
);

  wire Cout0, Cout1, Cout2, Cout3, Cout4, Cout5, Cout6;

  FullAdder fulladder_1 (.A(A_7__0[7]), .B(B_7__0[7]), .Cin(Cout6), .S(Sum_7__0[7]), .Cout(Final_Cout));
  FullAdder fulladder_2 (.A(A_7__0[6]), .B(B_7__0[6]), .Cin(Cout5), .S(Sum_7__0[6]), .Cout(Cout6));
  FullAdder fulladder_3 (.A(A_7__0[5]), .B(B_7__0[5]), .Cin(Cout4), .S(Sum_7__0[5]), .Cout(Cout5));
  FullAdder fulladder_4 (.A(A_7__0[4]), .B(B_7__0[4]), .Cin(Cout3), .S(Sum_7__0[4]), .Cout(Cout4));
  FullAdder fulladder_5 (.A(A_7__0[3]), .B(B_7__0[3]), .Cin(Cout2), .S(Sum_7__0[3]), .Cout(Cout3));
  FullAdder fulladder_6 (.A(A_7__0[2]), .B(B_7__0[2]), .Cin(Cout1), .S(Sum_7__0[2]), .Cout(Cout2));
  FullAdder fulladder_7 (.A(A_7__0[1]), .B(B_7__0[1]), .Cin(Cout0), .S(Sum_7__0[1]), .Cout(Cout1));
  FullAdder fulladder_8 (.A(A_7__0[0]), .B(B_7__0[0]), .Cin(Cin), .S(Sum_7__0[0]), .Cout(Cout0));

  // Other names for the same wires on the sheet: A0 = A_7__0[0]; A1 = A_7__0[1]; A2 = A_7__0[2]; A3 = A_7__0[3];
  //   A4 = A_7__0[4]; A5 = A_7__0[5]; A6 = A_7__0[6]; A7 = A_7__0[7]; B0 = B_7__0[0]; B1 = B_7__0[1]; B2 = B_7__0[2];
  //   B3 = B_7__0[3]; B4 = B_7__0[4]; B5 = B_7__0[5]; B6 = B_7__0[6]; B7 = B_7__0[7]; S0 = Sum_7__0[0];
  //   S1 = Sum_7__0[1]; S2 = Sum_7__0[2]; S3 = Sum_7__0[3]; S4 = Sum_7__0[4]; S5 = Sum_7__0[5]; S6 = Sum_7__0[6];
  //   S7 = Sum_7__0[7]
endmodule
