// Digital circuit 8bit_Subtract.dig as structural Verilog
module _8bit_Subtract (
  input  [7:0] A,
  input  [7:0] B,
  output [7:0] SUB
);

  wire [7:0] B_t;

  assign B_t = ~B;  // Not not_1, 8 bits wide
  _8bit_Adder _8bit_adder_1 (.A_7__0(A), .B_7__0(B_t), .Cin(1'b1), .Sum_7__0(SUB));  // open: Final_Cout
endmodule
