// Digital circuit 8bit_decrementor.dig as structural Verilog
module _8bit_decrementor (
  input  [7:0] A_in,
  output [7:0] S_out
);

  _8bit_Adder _8bit_adder_1 (.A_7__0(A_in), .B_7__0({8{1'b1}}), .Cin(1'b0), .Sum_7__0(S_out));  // open: Final_Cout
endmodule
