// Digital circuit FullAdder.dig as structural Verilog
module FullAdder (
  input  A,
  input  B,
  input  Cin,
  output S,
  output Cout
);

  wire Cout1, Cout2, halfadder_1_s;

  HalfAdder halfadder_1 (.A(A), .B(B), .S(halfadder_1_s), .Cout(Cout1));
  HalfAdder halfadder_2 (.A(halfadder_1_s), .B(Cin), .S(S), .Cout(Cout2));
  or or_1 (Cout, Cout1, Cout2);
endmodule
