// Digital circuit PC.dig as structural Verilog
module PC (
  input  CLK,
  input  RST,
  input  EN,
  input  [3:0] Jump_addr,
  input  LOAD,
  output [3:0] C_OUT
);

  wire En_out;
  wire [3:0] M_out, M_outR, S_out;

  Multiplexer #(.Bits(4)) multiplexer_1 (.sel(RST), .in_0(M_out), .in_1(4'b0000), .out(M_outR));
  Multiplexer #(.Bits(4)) multiplexer_2 (.sel(LOAD), .in_0(S_out), .in_1(Jump_addr), .out(M_out));
  or or_1 (En_out, EN, LOAD);
  Register #(.Bits(4)) register_1 (.D(M_outR), .C(CLK), .en(En_out), .Q(C_OUT));
  Add #(.Bits(4)) add_1 (.a(C_OUT), .b(4'b0001), .c_i(1'b0), .s(S_out));  // open: c_o

  // Other names for the same wires on the sheet: Q_out[3:0] = C_OUT
endmodule
